# Fritzing sketch AndroidFritzingSketch (saved by Fritzing 0.9.3b)
breadboards: 1

parts:
  LED1 = LED - 5mm [color="Red (633nm)" package="5 mm [THT]"]
  S1 = Pushbutton [package="[THT]"]
  Raspberry_Pi_1 = Raspberry Pi 3 [part_number=RPI-3-V1.2]
  R2 = Resistor [tolerance=±5% resistance=220 package="2512 [SMD]"]
  R3 = Resistor [tolerance=±5% resistance=220 package=THT]

nets:
  N1: LED1.cathode, R3.Pin_1
  N2: LED1.anode, Raspberry_Pi_1.GPIO3
  N3: S1.Pin_1, S1.Pin_2, Raspberry_Pi_1.GPIO2, R2.Pin_0
  N4: S1.Pin_3, S1.Pin_4, Raspberry_Pi_1.GND, R3.Pin_0
  N5: Raspberry_Pi_1.3v3, R2.Pin_1
