# Fritzing sketch CircuitSketch (saved by Fritzing 0.9.3b)
breadboards: 1

parts:
  Part1 = Arduino Uno (Rev3)
  S1 = Pushbutton [package="[THT]"]
  LED1 = smd LED [color="Red (633nm)" package="0805 [SMD]"]
  R1 = Resistor [tolerance=±5% resistance=1k package="2512 [SMD]"]

nets:
  N1: Part1.5V, S1.Pin_1, S1.Pin_2
  N2: Part1.GND, R1.Pin_1
  N3: S1.Pin_3, S1.Pin_4, LED1.anode
  N4: LED1.cathode, R1.Pin_0
